# Fritzing sketch FormulaOne (saved by Fritzing 0.9.0b)

parts:
  Part1 = Arduino Mega ADK (Rev3)
  ULN2 = Darlington Driver [package=so018]
  S1 = Momentary Switch [package=ksa_sealed_tac_switch]
  S2 = Momentary Switch [package=ksa_sealed_tac_switch]
  S3 = Momentary Switch [package=ksa_sealed_tac_switch]
  S4 = Momentary Switch [package=ksa_sealed_tac_switch]

nets:
  N1: Part1.GND, ULN2.9
  N2: Part1.D12_PWM, ULN2.2
  N3: Part1.D11_PWM, ULN2.3
  N4: Part1.D10_PWM, ULN2.4
  N5: Part1.D9_PWM, ULN2.5
  N6: Part1.3V3, ULN2.10
  N7: ULN2.14, S4.2
  N8: ULN2.15, S3.4
  N9: ULN2.16, S2.4
  N10: ULN2.17, S1.4
